# Fritzing sketch DS18B20 (saved by Fritzing 0.9.3b)
breadboards: 1

parts:
  Arduino = Arduino Uno (Rev3) - ICSP
  R1 = Resistor [tolerance=±5% resistance=4.7k package="0402 [SMD]"]
  DS18B20 = DS18B20 1-Wire Temperature Sensor [part_number=DS18B20]

nets:
  N1: Arduino.D2, R1.Pin_1, DS18B20.DQ
  5V: Arduino.5V, R1.Pin_0, DS18B20.VDD
  GND: Arduino.GND, DS18B20.GND
