# Fritzing sketch Rangkaian Lengkap (saved by Fritzing 0.9.3b)
breadboards: 1

parts:
  Arduino = Arduino Uno (Rev3) - ICSP
  R1 = Resistor [tolerance=±5% resistance=4.7k package="0402 [SMD]"]
  DS18B20 = DS18B20 1-Wire Temperature Sensor [part_number=DS18B20]
  Part1 = Real Time Clock Module - DS1307 RTC Breakout Board
  J1 = Basic Servo

nets:
  N1: Arduino.A4/SDA, Part1.SDA
  N2: Arduino.A5/SCL, Part1.SCL
  5V: Arduino.5V, R1.Pin_0, DS18B20.VDD, Part1.5V, J1.vcc
  N3: Arduino.D9_PWM, J1.pulse
  N4: Arduino.D2, R1.Pin_1, DS18B20.DQ
  GND: Arduino.GND, DS18B20.GND, Part1.GND, J1.gnd
